// Logisim project Domaci2.circ as structural Verilog: 2 circuits, main circuit minimizovano
module minimizovano (
  input  x1,
  input  x2,
  input  x3,
  input  x4,
  input  x5,
  output f
);

  wire and_1_out, and_2_out, and_4_out, not_1_out, not_2_out, not_3_out, not_4_out;

  not not_1 (not_1_out, x5);
  and and_1 (and_1_out, x2, not_1_out);
  not not_2 (not_2_out, x4);
  not not_3 (not_3_out, x3);
  not not_4 (not_4_out, x1);
  and and_2 (and_2_out, and_1_out, not_2_out);
  and and_3 (f, and_2_out, and_4_out);
  and and_4 (and_4_out, not_3_out, not_4_out);
endmodule

module Realizacija_sa_minimalnim_brojem_NILI_kola (
  input  x1,
  input  x2,
  input  x3,
  input  x4,
  input  x5,
  output f
);

  wire nor_1_out, nor_2_out, nor_3_out, nor_4_out, nor_5_out, nor_6_out, nor_7_out;

  nor nor_1 (nor_1_out, x2, x2);
  nor nor_2 (nor_2_out, nor_1_out, x5);
  nor nor_3 (nor_3_out, nor_2_out, nor_2_out);
  nor nor_4 (nor_4_out, nor_3_out, x4);
  nor nor_5 (nor_5_out, x3, x1);
  nor nor_6 (nor_6_out, nor_4_out, nor_4_out);
  nor nor_7 (nor_7_out, nor_5_out, nor_5_out);
  nor nor_8 (f, nor_6_out, nor_7_out);

  // Notes on the sheet:
  //   Datum rodjenja: 06.11. = 6 + 1 + 1 = 8
endmodule
